// Logisim project HEDA_MANUAL_FINISHED_FILE.circ as structural Verilog
// ALU
module ALU_Unwired (
  input  [7:0] Input_A,
  input  [7:0] Input_B,
  input  [2:0] OpSel,
  output V,
  output N,
  output [7:0] Result,
  output Z
);

  wire [7:0] adder_1_out, adder_2_out, and_1_out, not_1_out, or_1_out, shifter_1_out, shifter_2_out,
       subtractor_1_out;

  Adder adder_1 (.a(Input_A), .b(8'h1), .out(adder_1_out));  // open: cin, cout
  Adder adder_2 (.a(Input_A), .b(Input_B), .out(adder_2_out), .cout(V));  // open: cin
  Subtractor subtractor_1 (.a(Input_A), .b(Input_B), .out(subtractor_1_out));  // open: bin, bout
  assign and_1_out = Input_A & Input_B;  // AND_Gate and_1, 8 bits wide
  assign or_1_out = Input_A | Input_B;  // OR_Gate or_1, 8 bits wide
  assign not_1_out = ~Input_A;  // NOT_Gate not_1, 8 bits wide
  Shifter shifter_1 (.in(Input_A), .\dist (Input_B[2:0]), .out(shifter_1_out));
  Shifter #(.shift("lr")) shifter_2 (.in(Input_A), .\dist (Input_B[2:0]), .out(shifter_2_out));
  Multiplexer #(.select(3), .width(8), .enable("false")) multiplexer_1 (
    .in0(adder_2_out), .in1(subtractor_1_out), .in2(and_1_out), .in3(or_1_out), .in4(not_1_out),
    .in5(shifter_1_out), .in6(shifter_2_out), .in7(adder_1_out), .out({N, Result[6:0]}), .sel(OpSel));
  Comparator #(.mode("unsigned")) comparator_1 (.a({N, Result[6:0]}), .b({8{1'b0}}), .eq(Z));  // open: gt, lt

  assign Result[7] = N;

  // Notes on the sheet:
  //   Operand A (8-bit)
  //   Operand B (8-bit)
  //   Operation Select Code (3-bit)
  //   Use for Shifter 'Distance' input
  //   Shift Distance Extractor (Lower 3 bits)
  //   Arithmetic Addition Unit
  //   Arithmetic Subtraction Unit
  //   Bitwise Logic Array
  //   Barrel Shifters (Left/Right)
  //   HEDA-8 Arithmetic Logic Unit (ALU) Schematic
  //   8-to-1 Operation MUX
  //   Overflow Flag (V)
  //   Negative Flag (N) - MSB Check
  //   Zero Flag (Z) - Zero Comparator
  //   ALU Main Output (to Bus)
endmodule

module CPU_Main (
  input  ENABLE_A,
  input  [7:0] in_2,
  input  Write_B,
  input  Write_C,
  input  Write_D,
  input  Write_PC,
  input  Write_IR,
  input  Write_MAR,
  input  in_9,
  input  MBR_EN,
  input  in_11,
  input  [2:0] OpCode_Select
);

  wire button_1_out, button_2_out, button_3_out, button_4_out, button_5_out, button_6_out, button_7_out,
       button_8_out, button_9_out, button_10_out, button_11_out;
  wire [7:0] alu_unwired_1_result, ram_1_data, register_1_q, register_2_q, register_3_q, register_4_q,
       register_5_q, register_6_q, register_7_q, register_8_q, register_9_q, register_10_q;

  Button button_1 (.out(button_1_out));
  RAM_part #(.bus("separate")) ram_1 (
    .addr(register_9_q), .din(in_2), .data(ram_1_data), .str(1'b1), .sel(1'b1), .clk(button_1_out),
    .ld(1'b1), .clr(1'b0));
  Register_part register_1 (.D(in_2), .Q(register_1_q), .clk(button_2_out));  // open: en, clr
  Button button_2 (.out(button_2_out));
  Button button_3 (.out(button_3_out));
  Register_part register_2 (.D(in_2), .en(1'b1), .Q(register_2_q), .clk(button_4_out), .clr(1'b0));
  Button button_4 (.out(button_4_out));
  assign in_2 = Write_B ? register_2_q : 8'bz;  // Controlled_Buffer controlled_buffer_1
  Register_part register_3 (.D(in_2), .en(1'b1), .Q(register_3_q), .clk(button_5_out), .clr(1'b0));
  Button button_5 (.out(button_5_out));
  assign in_2 = Write_C ? register_3_q : 8'bz;  // Controlled_Buffer controlled_buffer_2
  Register_part register_4 (.D(in_2), .en(1'b1), .Q(register_4_q), .clk(button_6_out), .clr(1'b0));
  Button button_6 (.out(button_6_out));
  assign in_2 = Write_D ? register_4_q : 8'bz;  // Controlled_Buffer controlled_buffer_3
  Register_part register_5 (.D(in_2), .en(1'b1), .Q(register_5_q), .clk(button_7_out), .clr(1'b0));
  Button button_7 (.out(button_7_out));
  assign in_2 = Write_PC ? register_5_q : 8'bz;  // Controlled_Buffer controlled_buffer_4
  Register_part register_6 (.D(in_2), .en(1'b1), .Q(register_6_q), .clk(button_8_out), .clr(1'b0));
  Button button_8 (.out(button_8_out));
  assign in_2 = Write_IR ? register_6_q : 8'bz;  // Controlled_Buffer controlled_buffer_5
  Button button_9 (.out(button_9_out));
  assign in_2 = in_9 ? ram_1_data : 8'bz;  // Controlled_Buffer controlled_buffer_6
  Button button_10 (.out(button_10_out));
  Register_part register_7 (.D(in_2), .Q(register_7_q), .clk(button_11_out));  // open: en, clr
  Button button_11 (.out(button_11_out));
  Register_part register_8 (.D(in_2), .Q(register_8_q), .clk(button_3_out));  // open: en, clr
  assign in_2 = ENABLE_A ? register_8_q : 8'bz;  // Controlled_Buffer controlled_buffer_7
  Register_part register_9 (.D(in_2), .en(1'b1), .Q(register_9_q), .clk(button_9_out), .clr(1'b0));
  assign in_2 = Write_MAR ? register_9_q : 8'bz;  // Controlled_Buffer controlled_buffer_8
  Register_part register_10 (.D(in_2), .en(1'b1), .Q(register_10_q), .clk(button_10_out), .clr(1'b0));
  assign in_2 = MBR_EN ? register_10_q : 8'bz;  // Controlled_Buffer controlled_buffer_9
  assign in_2 = in_11 ? alu_unwired_1_result : 8'bz;  // Controlled_Buffer controlled_buffer_10
  ALU_Unwired alu_unwired_1 (
    .Input_A(register_7_q), .Input_B(register_1_q), .OpSel(OpCode_Select), .Result(alu_unwired_1_result));  // open: V, N, Z
  // Probe on alu_unwired_1_result

  // Notes on the sheet:
  //   Address Bus (from MAR)
  //   Main Memory (256x8 RAM)
  //   RAM_CS
  //   Data Bus (Write)
  //   RAM_CLR
  //   MEM WRITE
  //   ALU Input A (Latch)
  //   ALU Input B (Latch
  //   Write A
  //   BUS_DEBUG
  //   ENABLE B
  //   ENABLE C
  //   ENABLE D
  //   	PC_EN
  //   	IR_EN
  //   	MAR_EN
  //   Memory Address Register
  //   Instruction Register
  //   Memory Buffer Register
  //   REGISTER A
  //   REGISTER B
  //   REGISTER C
  //   REGISTER D
  //   PROGRAM COUNTER
  //   ALU Output Enable
  //   HEDA-8 Architecture: 8-Bit CPU Datapath
  //   VERTICAL DATA_BUS
endmodule

module Register (
  input  Write_A,
  input  [7:0] in_2
);

  wire button_1_out;
  wire [7:0] register_1_q;

  Register_part register_1 (.D(in_2), .en(1'b1), .Q(register_1_q), .clk(button_1_out), .clr(1'b0));
  Button button_1 (.out(button_1_out));
  assign in_2 = Write_A ? register_1_q : 8'bz;  // Controlled_Buffer controlled_buffer_1

  // Notes on the sheet:
  //   ENABLE A
endmodule

module RAM (
  input  Write_MAR,
  input  in_2,
  input  MBR_EN
);

  wire button_1_out, button_2_out, clock_1_out, undriven;
  wire [7:0] controlled_buffer_1_out, ram_1_data, register_1_q, register_2_q;

  Clock clock_1 (.out(clock_1_out));
  RAM_part #(.bus("separate")) ram_1 (
    .addr(register_1_q), .din(register_1_q), .data(ram_1_data), .str(undriven), .sel(1'b1),
    .clk(clock_1_out), .ld(1'b1), .clr(1'b0));
  Register_part register_1 (.D(controlled_buffer_1_out), .en(1'b1), .Q(register_1_q), .clk(button_1_out), .clr(1'b0));
  Button button_1 (.out(button_1_out));
  assign controlled_buffer_1_out = Write_MAR ? register_1_q : 8'bz;  // Controlled_Buffer controlled_buffer_1
  Controlled_Buffer #(.width(8)) controlled_buffer_2 (.in(ram_1_data), .en(in_2));  // open: out
  Register_part register_2 (.D(register_1_q), .en(1'b1), .Q(register_2_q), .clk(button_2_out), .clr(1'b0));
  Button button_2 (.out(button_2_out));
  assign register_1_q = MBR_EN ? register_2_q : 8'bz;  // Controlled_Buffer controlled_buffer_3

  // Notes on the sheet:
  //   Address Bus (from MAR)
  //   RAM_CS
  //   Data Bus (Write)
  //   Main Memory (256x8 RAM)
  //   RAM_CLR
  //   CLK
  //   	MAR_EN
  //   Memory Buffer Register
  //   VERTICAL BUS 
endmodule
