// Logisim project HEDA_AUTO_FINISHED_FILE.circ as structural Verilog: 5 circuits, main circuit CPU_Main
// ALU
module ALU_Unwired (
  input  [7:0] Input_A,
  input  [7:0] Input_B,
  input  [2:0] OpSel,
  output V,
  output N,
  output [7:0] Result,
  output Z
);

  wire [7:0] adder_1_out, adder_2_out, and_1_out, not_1_out, or_1_out, shifter_1_out, shifter_2_out,
       subtractor_1_out;

  Adder adder_1 (.a(Input_A), .b(8'h1), .out(adder_1_out));  // open: cin, cout
  Adder adder_2 (.a(Input_A), .b(Input_B), .out(adder_2_out), .cout(V));  // open: cin
  Subtractor subtractor_1 (.a(Input_A), .b(Input_B), .out(subtractor_1_out));  // open: bin, bout
  assign and_1_out = Input_A & Input_B;  // AND_Gate and_1, 8 bits wide
  assign or_1_out = Input_A | Input_B;  // OR_Gate or_1, 8 bits wide
  assign not_1_out = ~Input_A;  // NOT_Gate not_1, 8 bits wide
  Shifter shifter_1 (.in(Input_A), .\dist (Input_B[2:0]), .out(shifter_1_out));
  Shifter #(.shift("lr")) shifter_2 (.in(Input_A), .\dist (Input_B[2:0]), .out(shifter_2_out));
  Multiplexer #(.select(3), .width(8), .enable("false")) multiplexer_1 (
    .in0(adder_2_out), .in1(subtractor_1_out), .in2(and_1_out), .in3(or_1_out), .in4(not_1_out),
    .in5(shifter_1_out), .in6(shifter_2_out), .in7(adder_1_out), .out({N, Result[6:0]}), .sel(OpSel));
  Comparator #(.mode("unsigned")) comparator_1 (.a({N, Result[6:0]}), .b({8{1'b0}}), .eq(Z));  // open: gt, lt

  assign Result[7] = N;

  // Notes on the sheet:
  //   Operand A (8-bit)
  //   Operand B (8-bit)
  //   Operation Select Code (3-bit)
  //   Use for Shifter 'Distance' input
  //   Shift Distance Extractor (Lower 3 bits)
  //   Arithmetic Addition Unit
  //   Arithmetic Subtraction Unit
  //   Bitwise Logic Array
  //   Barrel Shifters (Left/Right)
  //   HEDA-8 Arithmetic Logic Unit (ALU) Schematic
  //   8-to-1 Operation MUX
  //   Overflow Flag (V)
  //   Negative Flag (N) - MSB Check
  //   Zero Flag (Z) - Zero Comparator
  //   ALU Main Output (to Bus)
endmodule

module CPU_Main (
  input  [7:0] in_1
);

  wire CLK_out, control_1_alu_enable_out, control_1_en_pc, control_1_enable_a, control_1_enable_b,
       control_1_mem_read, control_1_write_a, control_1_write_ir, control_1_write_latch_a,
       control_1_write_latch_b, control_1_write_mar, RES_out;
  wire [7:0] alu_unwired_1_result, ram_1_data, register_1_q, register_2_q, register_3_q, register_4_q,
       register_5_q, register_6_q, register_7_q, register_8_q, register_9_q, register_10_q;

  Control control_1 (
    .RESET(RES_out), .OpCode_In(register_7_q[2:0]), .EN_PC(control_1_en_pc), .WRITE_MAR(control_1_write_mar),
    .MEM_READ(control_1_mem_read), .WRITE_IR(control_1_write_ir), .ENABLE_A(control_1_enable_a),
    .WRITE_LATCH_A(control_1_write_latch_a), .ENABLE_B(control_1_enable_b),
    .WRITE_LATCH_B(control_1_write_latch_b), .ALU_ENABLE_OUT(control_1_alu_enable_out),
    .WRITE_A(control_1_write_a));
  Clock CLK (.out(CLK_out));
  Button RES (.out(RES_out));
  RAM_part #(.bus("separate")) ram_1 (
    .addr(register_8_q), .din(in_1), .data(ram_1_data), .str(1'b0), .sel(1'b1), .clk(1'b0), .ld(1'b1),
    .clr(1'b0));
  assign in_1 = control_1_mem_read ? ram_1_data : 8'bz;  // Controlled_Buffer controlled_buffer_1
  Register_part register_1 (.D(in_1), .Q(register_1_q), .clk(control_1_write_latch_b));  // open: en, clr
  Register_part register_2 (.D(in_1), .Q(register_2_q), .clk(control_1_write_a), .clr(1'b0));  // open: en
  assign in_1 = control_1_enable_a ? register_2_q : 8'bz;  // Controlled_Buffer controlled_buffer_2
  Register_part register_3 (.D(in_1), .en(1'b1), .Q(register_3_q), .clk(1'b0), .clr(1'b0));
  assign in_1 = control_1_enable_b ? register_3_q : 8'bz;  // Controlled_Buffer controlled_buffer_3
  Register_part register_4 (.D(in_1), .en(1'b1), .Q(register_4_q), .clk(1'b0), .clr(1'b0));
  assign in_1 = 1'b0 ? register_4_q : 8'bz;  // Controlled_Buffer controlled_buffer_4
  Register_part register_5 (.D(in_1), .en(1'b1), .Q(register_5_q), .clk(1'b0), .clr(1'b0));
  assign in_1 = 1'b0 ? register_5_q : 8'bz;  // Controlled_Buffer controlled_buffer_5
  Register_part register_6 (.D(in_1), .en(1'b1), .Q(register_6_q), .clr(control_1_en_pc));  // open: clk
  assign in_1 = control_1_en_pc ? register_6_q : 8'bz;  // Controlled_Buffer controlled_buffer_6
  Register_part register_7 (.D(in_1), .en(1'b1), .Q(register_7_q), .clk(control_1_write_ir), .clr(1'b0));
  assign in_1 = 1'b0 ? register_7_q : 8'bz;  // Controlled_Buffer controlled_buffer_7
  Register_part register_8 (.D(in_1), .en(1'b1), .Q(register_8_q), .clk(control_1_write_mar), .clr(1'b0));
  assign in_1 = 1'b0 ? register_8_q : 8'bz;  // Controlled_Buffer controlled_buffer_8
  Register_part register_9 (.D(in_1), .en(1'b1), .Q(register_9_q), .clk(1'b0), .clr(1'b0));
  assign in_1 = 1'b0 ? register_9_q : 8'bz;  // Controlled_Buffer controlled_buffer_9
  Register_part register_10 (.D(in_1), .Q(register_10_q), .clk(control_1_write_latch_a));  // open: en, clr
  ALU_Unwired alu_unwired_1 (
    .Input_A(register_10_q), .Input_B(register_1_q), .OpSel(register_7_q[2:0]), .Result(alu_unwired_1_result));  // open: V, N, Z
  assign in_1 = control_1_alu_enable_out ? alu_unwired_1_result : 8'bz;  // Controlled_Buffer controlled_buffer_10
  // Probe on alu_unwired_1_result
  // also tied to GND on the sheet: control_1_en_pc

  // Notes on the sheet:
  //   Address Bus (from MAR)
  //   RAM_CS
  //   Data Bus (Write)
  //   Main Memory (256x8 RAM)
  //   RAM_CLR
  //   ALU Input A (Latch)
  //   ALU Input B (Latch
  //   ENABLE B
  //   Write C
  //   ENABLE C
  //   ENABLE D
  //   	PC_EN
  //   	IR_EN
  //   Write A
  //   ENABLE A
  //   Write IR
  //   Write MAR
  //   	MAR_EN
  //   Memory Buffer Register
  //   REGISTER B
  //   REGISTER C
  //   REGISTER D
  //   REGISTER A
  //   PROGRAM COUNTER
  //   HEDA-8 Architecture: 8-Bit CPU Datapath
  //   VERTICAL DATA_BUS
endmodule

module Register (
  input  Write_A,
  input  [7:0] in_2
);

  wire button_1_out;
  wire [7:0] register_1_q;

  Register_part register_1 (.D(in_2), .en(1'b1), .Q(register_1_q), .clk(button_1_out), .clr(1'b0));
  Button button_1 (.out(button_1_out));
  assign in_2 = Write_A ? register_1_q : 8'bz;  // Controlled_Buffer controlled_buffer_1

  // Notes on the sheet:
  //   ENABLE A
endmodule

module RAM (
  input  Write_MAR,
  input  in_2,
  input  MBR_EN
);

  wire button_1_out, button_2_out, clock_1_out, undriven;
  wire [7:0] controlled_buffer_1_out, ram_1_data, register_1_q, register_2_q;

  Clock clock_1 (.out(clock_1_out));
  RAM_part #(.bus("separate")) ram_1 (
    .addr(register_1_q), .din(register_1_q), .data(ram_1_data), .str(undriven), .sel(1'b1),
    .clk(clock_1_out), .ld(1'b1), .clr(1'b0));
  Register_part register_1 (.D(controlled_buffer_1_out), .en(1'b1), .Q(register_1_q), .clk(button_1_out), .clr(1'b0));
  Button button_1 (.out(button_1_out));
  assign controlled_buffer_1_out = Write_MAR ? register_1_q : 8'bz;  // Controlled_Buffer controlled_buffer_1
  Controlled_Buffer #(.width(8)) controlled_buffer_2 (.in(ram_1_data), .en(in_2));  // open: out
  Register_part register_2 (.D(register_1_q), .en(1'b1), .Q(register_2_q), .clk(button_2_out), .clr(1'b0));
  Button button_2 (.out(button_2_out));
  assign register_1_q = MBR_EN ? register_2_q : 8'bz;  // Controlled_Buffer controlled_buffer_3

  // Notes on the sheet:
  //   Address Bus (from MAR)
  //   RAM_CS
  //   Data Bus (Write)
  //   Main Memory (256x8 RAM)
  //   RAM_CLR
  //   CLK
  //   	MAR_EN
  //   Memory Buffer Register
  //   VERTICAL BUS 
endmodule

// CONTROL
module Control (
  input  RESET,
  input  [2:0] OpCode_In,
  output EN_PC,
  output WRITE_MAR,
  output MEM_READ,
  output WRITE_IR,
  output ENABLE_A,
  output WRITE_LATCH_A,
  output ENABLE_B,
  output WRITE_LATCH_B,
  output ALU_ENABLE_OUT,
  output WRITE_A
);

  wire clock_1_out, decoder_1_out2, decoder_1_out3, decoder_1_out4, decoder_2_out0, decoder_2_out1,
       decoder_2_out2, decoder_2_out3, decoder_2_out4, decoder_2_out5, decoder_2_out6, or_1_out;
  wire [2:0] counter_1_q;

  Counter #(.width(3), .max('h7)) counter_1 (
    .Q(counter_1_q), .clk(clock_1_out), .clr(RESET));  // open: load, D, count, carry
  Clock clock_1 (.out(clock_1_out));
  Decoder #(.select(3), .tristate("true"), .enable("false")) decoder_1 (
    .out0(EN_PC), .out1(MEM_READ), .out2(decoder_1_out2), .out3(decoder_1_out3), .out4(decoder_1_out4),
    .sel(counter_1_q));  // open: out5, out6, out7
  Decoder #(.select(3), .enable("false")) decoder_2 (
    .out0(decoder_2_out0), .out1(decoder_2_out1), .out2(decoder_2_out2), .out3(decoder_2_out3),
    .out4(decoder_2_out4), .out5(decoder_2_out5), .out6(decoder_2_out6), .sel(OpCode_In));  // open: out7
  or or_1 (or_1_out, decoder_2_out0, decoder_2_out1, decoder_2_out2, decoder_2_out3, decoder_2_out4, decoder_2_out5, decoder_2_out6);
  Multiplexer #(.enable("false")) multiplexer_1 (.in0(1'b0), .in1(or_1_out), .out(ENABLE_A), .sel(decoder_1_out2));
  Multiplexer #(.enable("false")) multiplexer_2 (.in0(1'b0), .in1(or_1_out), .out(ENABLE_B), .sel(decoder_1_out3));
  Multiplexer #(.enable("false")) multiplexer_3 (
    .in0(or_1_out), .in1(1'b1), .out(ALU_ENABLE_OUT), .sel(decoder_1_out4));

  assign WRITE_A = ALU_ENABLE_OUT;
  assign WRITE_IR = MEM_READ;
  assign WRITE_LATCH_A = ENABLE_A;
  assign WRITE_LATCH_B = ENABLE_B;
  assign WRITE_MAR = EN_PC;

  // Notes on the sheet:
  //   CLK
  //   T0
  //   T1
  //   T2
  //   T3
  //   T4
  //   T5
  //   T6
  //   T7
  //   ADD
  //   SUB
  //   AND
  //   OR
  //   NOT
  //   SHL
  //   SHR
  //   INC
endmodule
